# Fritzing sketch motor (saved by Fritzing 0.9.3b)
breadboards: 1

parts:
  Raspberry_Pi1 = Raspberry Pi B+
  VCC1 = Battery
  IC1 = L293D [package=THT]
  M1 = DC Motor
  M2 = DC Motor

nets:
  N1: Raspberry_Pi1.GPIO17, IC1.Enable_2
  N2: Raspberry_Pi1.GPIO27, IC1.In_3
  N3: Raspberry_Pi1.GPIO22, IC1.In_4
  N4: Raspberry_Pi1.GPIO25, IC1.In_1
  N5: Raspberry_Pi1.GPIO24, IC1.Enable_1
  N6: Raspberry_Pi1.GPIO23, IC1.In_2
  N7: Raspberry_Pi1.GND, VCC1.-, IC1.0V
  N8: Raspberry_Pi1.5V, IC1.+V
  N9: VCC1.+, IC1.+Vmotor
  N10: IC1.Out_1_(_Controlled_by_Enable_1_), M1.pin_2
  N11: IC1.Out_2_(_Controlled_by_Enable_1_), M1.pin_1
  N12: IC1.Out_3_(_Controlled_by_Enable_2_), M2.pin_1
  N13: IC1.Out_4_(_Controlled_by_Enable_2_), M2.pin_2
